// Logisim project Ctl_Data_Processing.circ as structural Verilog: 1 circuit, main circuit Data_Processing
module Data_Processing (
  input  Enable,
  input  [15:0] Instruction,
  output [2:0] Rd,
  output [2:0] Rn,
  output [2:0] Rm,
  output [3:0] ALU_Opcode,
  output [3:0] Flags_Update_Mask
);

  wire ANDS;

  and and_1 (ANDS, ~Instruction[6], ~Instruction[7], ~Instruction[8], ~Instruction[9]);  // AND_Gate
  and and_2 (ANDS, ~Instruction[6], ~Instruction[7], ~Instruction[8], ~Instruction[9]);  // AND_Gate
  and and_3 (ANDS, ~Instruction[6], ~Instruction[7], ~Instruction[8], ~Instruction[9]);  // AND_Gate

  // Other names for the same wires on the sheet: OP_IN[15:0] = Instruction

  // Notes on the sheet:
  //   Note 2: RSB instruction has Rn as 1st operand.
  //   MUL instruction has Rn as 1st operand and Rdm as 2nd operand
  //   For simplification purposes, Rm is used for 1st operand both here and in the ALU.
  //   Note: instructions that does not save the result will still have the second operand as the destination register, the ALU will copy the second register to the destination register
  //   Pull output low on Enable = 0
endmodule
